// Logisim project hadd.circ as structural Verilog: 1 circuit, main circuit main
module main (
  input  in_1,
  input  in_2,
  output sum,
  output carry
);

  xor xor_1 (sum, in_1, in_2);
  and and_1 (carry, in_2, in_1);
endmodule
