// Logisim project halfsub.circ as structural Verilog: 1 circuit, main circuit main
module main (
  input  in_1,
  input  in_2,
  output Diff,
  output Borrow
);

  wire not_1_out;

  not not_1 (not_1_out, in_1);
  xor xor_1 (Diff, in_1, in_2);
  and and_1 (Borrow, not_1_out, in_2);
endmodule
